# Fritzing sketch FenceJointsBTooth (saved by Fritzing 0.9.2b)
circuit board: 7cm x 5.8cm
breadboards: 1

parts:
  Part1 = Arduino Uno (Rev3)
  R1 = Resistor [tolerance=±5% resistance=33k package=THT]
  R2 = Resistor [tolerance=±5% resistance=15k package=THT]
  Part2 = Bluetooth HC-05 Macho
  J1 = female pin header, 6 pins [form="♀ (female)"]
  J2 = female pin header, 2 pins [form="♀ (female)"]
  J3 = female pin header, 4 pins [form="♀ (female)"]
  J4 = female pin header, 2 pins [form="♀ (female)"]
  S1 = H-Bridge with L298N
  M1 = DC Motor

nets (from the pcb view):
  N1: Part1.D8, J1.pin4
  N2: Part1.D9_PWM, J1.pin5
  N3: Part1.D10_PWM/SS, J1.pin6
  GND: Part1.GND, R1.Pin_0, Part2.GND, J3.pin3, J3.pin4
  N4: Part1.D0/RX, J4.pin1
  N5: Part1.D1/TX, R2.Pin_1
  N6: Part1.D2, J2.pin1
  N7: Part1.D3_PWM, J2.pin2
  N8: Part1.D5_PWM, J1.pin1
  N9: Part1.D6_PWM, J1.pin2
  N10: Part1.D7, J1.pin3
  5V: Part1.5V, Part2.VCC, J3.pin1, J3.pin2
  N11: R1.Pin_1, R2.Pin_0, Part2.RXD
  N12: Part2.TXD, J4.pin2
  N13: S1.M2-02, M1.pin_1

custom parts:
  H-Bridge with L298N: h-bridge
